# Fritzing sketch st7735 (saved by Fritzing 0.9.3b)

parts:
  Raspberry_Pi_1 = Raspberry Pi 3 [part_number=RPI-3-V1.2]
  Composant1 = TFT 1.8 inch 160x128 w microSD [part_number=358]

nets:
  N1: Raspberry_Pi_1.GIPO10, Composant1.MOSI
  N2: Raspberry_Pi_1.GIPO11, Composant1.SCLK
  N3: Raspberry_Pi_1.GIPO8, Composant1.TFTCS
  N4: Raspberry_Pi_1.GIPO25, Composant1.RESET
  N5: Raspberry_Pi_1.GIPO24, Composant1.TFTDC
  GND: Raspberry_Pi_1.GND, Composant1.GND
  5V: Raspberry_Pi_1.5V, Composant1.+5V

custom parts:
  TFT 1.8 inch 160x128 w microSD: This lovely little display breakout is the best way to add a small, colorful and bright display to any project. Since the display uses 4-wire SPI to communicate and has its own pixel-addressable frame buffer, it can be used with every kind of microcontroller. Even a very small one with low memory and few pins available! The 1.8" display has 128x160 color pixels.
